# Fritzing sketch RoomMonitoringWiring (saved by Fritzing 0.9.4)

parts:
  Part1 = Arduino Nano 33 IOT
  GY-1 = GY-302 [part_number=GY-302]
  DHT1 = DHT11 Humitidy and Temperature Sensor (3 pins)

nets:
  GND: Part1.GND, Part1.D13~, GY-1.GND, DHT1.Gnd
  N1: Part1.D2, DHT1.Signal
  N2: Part1.A5, GY-1.SCL
  N3: Part1.A4, GY-1.SDA
  3V3: Part1.3V3, GY-1.VCC, DHT1.Plus

custom parts:
  Arduino Nano 33 IOT: The Arduino Nano 33 IoT is the easiest and cheapest point of entry to enhance existing devices (and creating new ones) to be part of the IoT and designing pico-network applications. Whether you are looking at building a sensor network connected to your office or home router, or if you want to create a BLE device sending data to a cellphone, the Nano 33 IoT is your one-stop-solution for many of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
  DHT11 Humitidy and Temperature Sensor (3 pins): DHT11 Humidity and Temperature Sensor (3 pins).
